# Fritzing sketch ShiftRegister (saved by Fritzing 0.9.0b)

parts:
  U1 = 74HC595 [package="DIP16 [THT]"]
  Composant1 = Spark Core (v1.0)

nets:
  N1: U1.Q0, Composant1.D1
  N2: U1.VCC, Composant1.D0
