# Fritzing sketch ShiftRegister_Breadboard (saved by Fritzing 0.9.0b)
breadboards: 2

parts:
  U1 = 74HC595 [package="DIP16 [THT]"]
  U2 = 74HC595 [package="DIP16 [THT]"]  # not connected
  Composant1 = Spark Core (v1.0)

nets:
  VCC: U1.MR, U1.VCC, Composant1.3V3
  N1: U1.SH_CP, Composant1.D2
  N2: U1.ST_CP, Composant1.D1
  N3: U1.OE, Composant1.GND
  N4: U1.DS, Composant1.D0
